# Fritzing sketch Esp32CanBusRelayBoard (saved by Fritzing 0.9.3b)

parts:
  M1 = DOIT Esp32 DevKit v1 (30 pins long, 11 pins width) [part_number=ESP32S-PIN30]
  U1 = 4-Channel 5v Relay Shield [package=relay-4ch5v10a]
  M2 = RioRand LM2596
  J1 = Camdenboss CTB0158-3 [part_number=CTB0158-3 package=THT]
  J3 = screw terminal, 3 pins
  J5 = Camdenboss CTB0158-3 [part_number=CTB0158-3 package=THT]
  J6 = Camdenboss CTB0158-3 [part_number=CTB0158-3 package=THT]
  J7 = Camdenboss CTB0158-3 [part_number=CTB0158-3 package=THT]
  J8 = Camdenboss CTB0158-3 [part_number=CTB0158-3 package=THT]
  J9 = Camdenboss CTB0158-4 [part_number=CTB0158-4 package=THT]
  JP1 = Jumper [package=sj_2s]
  U2 = RELAY [package=relay-g5q]
  J10 = Camdenboss CTB0158-5 [part_number=CTB0158-5 package=THT]
  M3 = SN65HVD230 CAN Bus transciever module [package=THT]

nets:
  3V3: M1.3V3, U1.VCC, M3.pin_1
  GND: M1.GND, U1.GND, M2.Pin_4, J1.terminal_1, J5.terminal_1, J6.terminal_1, J7.terminal_1, J8.terminal_1, J9.terminal_1, M3.pin_2
  N1: M1.D15, U1.IN4
  N2: M1.D2, U1.IN3
  N3: M1.D4, U1.IN2
  N4: M1.RX2, U1.IN1
  N5: M1.D32, M3.pin_4
  N6: M1.D33, M3.pin_3
  N7: M1.D26, J5.terminal_3
  N8: M1.D27, J6.terminal_3
  N9: M1.D14, J7.terminal_3
  N10: M1.D12, J8.terminal_3
  N11: M1.D13, J1.terminal_3
  N12: M1.VIN, M2.Pin_3, J1.terminal_2, J5.terminal_2, J6.terminal_2, J7.terminal_2, J8.terminal_2, J9.terminal_2
  N13: U1.K1-In, U1.K2-In, U1.K3-In, U1.K4-In, J3.pin3, U2.MAIN
  N14: U1.K1-On, J10.pin4
  N15: U1.K2-On, J10.pin3
  N16: U1.K3-On, J10.pin2
  N17: U1.K4-On, J10.pin1
  N18: M2.Pin_1, U2.NO
  N19: M2.Pin_2, J3.pin1, U2.COIL2
  N20: J3.pin2, U2.COIL1
  N21: J9.terminal_3, JP1.2, M3.pin_5
  N22: J9.terminal_4, JP1.1, M3.pin_6

notes:
  Voltage divider for 3.3V Analog
  5V
  5V power & canbus
  120 ohm terminator resistor jumper
  12V +
  ScrewTerminal
  12V -
  12V switched
  12V ~1A
  Solenoids connector
  input
  5V analog sensors
  Normally Open
  Normally
  Open

custom parts:
  DOIT Esp32 DevKit v1 (30 pins long, 11 pins width): The DOIT Esp32 DevKit v1 is one of the development board created by DOIT to evaluate the ESP-WROOM-32 module. It is based on the ESP32 microcontroller that boasts Wifi, Bluetooth, Ethernet and Low Power support all in a single chip. (vanepp) made breadboard work, adjusted pin numbering and labels and reduced size of schematic and cleaned up pcb. This chip is 30pins long (2 x15) and 11 pins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
  4-Channel 5v Relay Shield: 4 Channel 5v Relay Shield w. 2x SPD-06VDC-SD-C
  SN65HVD230 CAN Bus transciever module: Bus Transceiver SN65HVD230 CAN Communication Module, for Arduino.
