# Fritzing sketch Wiring (saved by Fritzing 0.9.3b)

parts:
  Onderdeel1 = Arduino Uno (Rev3)
  Onderdeel2 = I2C level shifter bidirectional
  J1 = Screw terminal - 2 pins [package=THT]
  J2 = Screw terminal - 2 pins [package=THT]
  J4 = Screw terminal - 2 pins [package=THT]
  J5 = Screw terminal - 2 pins [package=THT]
  J6 = Screw terminal - 2 pins [package=THT]
  J7 = Screw terminal - 2 pins [package=THT]
  J8 = Screw terminal - 2 pins [package=THT]
  J9 = Screw terminal - 2 pins [package=THT]
  U1 = 4-Channel 5v Relay Shield [package=relay-4ch5v10a]
  J10 = Screw terminal - 2 pins [package=THT]
  U2 = RELAY [package=relay-g5q]  # not connected
  J11 = Screw terminal - 2 pins [package=THT]

nets:
  N1: Onderdeel1.A0, J8.pin2
  N2: Onderdeel1.A1, J8.pin1
  N3: Onderdeel1.A2, J9.pin2
  N4: Onderdeel1.A3, J9.pin1
  N5: Onderdeel1.A4/SDA, J11.pin2
  N6: Onderdeel1.A5/SCL, J11.pin1
  GND: Onderdeel1.GND, Onderdeel2.GND, J2.pin1, J4.pin2, J5.pin1, J7.pin1, U1.GND
  N7: Onderdeel1.D0/RX, Onderdeel2.HV1
  N8: Onderdeel1.D1/TX, Onderdeel2.HV2
  N9: Onderdeel1.D4, U1.IN4
  N10: Onderdeel1.D5_PWM, U1.IN3
  N11: Onderdeel1.D6_PWM, U1.IN2
  N12: Onderdeel1.D7, U1.IN1
  N13: Onderdeel1.3V3, Onderdeel2.LV
  5V: Onderdeel1.5V, Onderdeel2.HV, J2.pin2, J7.pin2, U1.VCC
  N14: Onderdeel1.VIN, J5.pin2, U1.K1-In, U1.K2-In, U1.K3-In, U1.K4-In
  N15: Onderdeel2.LV2, J6.pin1
  N16: Onderdeel2.LV1, J6.pin2
  N17: J1.pin1, U1.K2-On
  N18: J1.pin2, U1.K3-On
  N19: J4.pin1, U1.K4-On
  N20: U1.K1-On, J10.pin2

notes:
  ESP32
  12V in
  Sensors
  Solenoids
  relay currently used
  UART Level Shifter
  Screw Terminals
  COM
  NO for all four wires

custom parts:
  4-Channel 5v Relay Shield: 4 Channel 5v Relay Shield w. 2x SPD-06VDC-SD-C
